// Logisim project RISCV.circ as structural Verilog: 18 circuits, main circuit PC
module PC (
  input  [23:0] inPC,
  input  CLK,
  input  R,
  output [23:0] outPCPlus1,
  output [23:0] outPC
);

  Register #(.width(24)) register_1 (.D(inPC), .en(1'b1), .clk(CLK), .Q(outPC), .clr(R));
  Adder #(.width(24)) adder_1 (.a(outPC), .b(24'h1), .out(outPCPlus1));  // open: cin, cout
endmodule

module RegisterFile (
  input  [4:0] rsi1,
  input  [4:0] rsi2,
  input  [4:0] rdi,
  input  [31:0] rd,
  input  we,
  input  CLK,
  input  R,
  output [31:0] rs1,
  output [31:0] rs2
);

  wire r0_we, r1_we, r2_we, r3_we, r4_we, r5_we, r6_we, r7_we, r8_we, r9_we, r10_we, r11_we, r12_we, r13_we,
       r14_we, r15_we, r16_we, r17_we, r18_we, r19_we, r20_we, r21_we, r22_we, r23_we, r24_we, r25_we,
       r26_we, r27_we, r28_we, r29_we, r30_we, r31_we;
  wire [31:0] x1q, x2q, x3q, x4q, x5q, x6q, x7q, x8q, x9q, x10q, x11q, x12q, x13q, x14q, x15q, x16q, x17q,
       x18q, x19q, x20q, x21q, x22q, x23q, x24q, x25q, x26q, x27q, x28q, x29q, x30q, x31q;

  Demultiplexer #(.select(5)) demultiplexer_1 (
    .out0(r0_we), .out1(r1_we), .out2(r2_we), .out3(r3_we), .out4(r4_we), .out5(r5_we), .out6(r6_we),
    .out7(r7_we), .out8(r8_we), .out9(r9_we), .out10(r10_we), .out11(r11_we), .out12(r12_we), .out13(r13_we),
    .out14(r14_we), .out15(r15_we), .out16(r16_we), .out17(r17_we), .out18(r18_we), .out19(r19_we),
    .out20(r20_we), .out21(r21_we), .out22(r22_we), .out23(r23_we), .out24(r24_we), .out25(r25_we),
    .out26(r26_we), .out27(r27_we), .out28(r28_we), .out29(r29_we), .out30(r30_we), .out31(r31_we), .in(we),
    .sel(rdi));
  Register #(.width(32)) x4 (.D(rd), .en(r4_we), .clk(CLK), .Q(x4q), .clr(R));
  Register #(.width(32)) x8 (.D(rd), .en(r8_we), .clk(CLK), .Q(x8q), .clr(R));
  Register #(.width(32)) x12 (.D(rd), .en(r12_we), .clk(CLK), .Q(x12q), .clr(R));
  Register #(.width(32)) x16 (.D(rd), .en(r16_we), .clk(CLK), .Q(x16q), .clr(R));
  Register #(.width(32)) x20 (.D(rd), .en(r20_we), .clk(CLK), .Q(x20q), .clr(R));
  Register #(.width(32)) x24 (.D(rd), .en(r24_we), .clk(CLK), .Q(x24q), .clr(R));
  Register #(.width(32)) x28 (.D(rd), .en(r28_we), .clk(CLK), .Q(x28q), .clr(R));
  Register #(.width(32)) x1 (.D(rd), .en(r1_we), .clk(CLK), .Q(x1q), .clr(R));
  Register #(.width(32)) x5 (.D(rd), .en(r5_we), .clk(CLK), .Q(x5q), .clr(R));
  Register #(.width(32)) x9 (.D(rd), .en(r9_we), .clk(CLK), .Q(x9q), .clr(R));
  Register #(.width(32)) x13 (.D(rd), .en(r13_we), .clk(CLK), .Q(x13q), .clr(R));
  Register #(.width(32)) x17 (.D(rd), .en(r17_we), .clk(CLK), .Q(x17q), .clr(R));
  Register #(.width(32)) x21 (.D(rd), .en(r21_we), .clk(CLK), .Q(x21q), .clr(R));
  Register #(.width(32)) x25 (.D(rd), .en(r25_we), .clk(CLK), .Q(x25q), .clr(R));
  Register #(.width(32)) x29 (.D(rd), .en(r29_we), .clk(CLK), .Q(x29q), .clr(R));
  Register #(.width(32)) x2 (.D(rd), .en(r2_we), .clk(CLK), .Q(x2q), .clr(R));
  Register #(.width(32)) x6 (.D(rd), .en(r6_we), .clk(CLK), .Q(x6q), .clr(R));
  Register #(.width(32)) x10 (.D(rd), .en(r10_we), .clk(CLK), .Q(x10q), .clr(R));
  Register #(.width(32)) x14 (.D(rd), .en(r14_we), .clk(CLK), .Q(x14q), .clr(R));
  Register #(.width(32)) x18 (.D(rd), .en(r18_we), .clk(CLK), .Q(x18q), .clr(R));
  Register #(.width(32)) x22 (.D(rd), .en(r22_we), .clk(CLK), .Q(x22q), .clr(R));
  Register #(.width(32)) x26 (.D(rd), .en(r26_we), .clk(CLK), .Q(x26q), .clr(R));
  Register #(.width(32)) x30 (.D(rd), .en(r30_we), .clk(CLK), .Q(x30q), .clr(R));
  Register #(.width(32)) x3 (.D(rd), .en(r3_we), .clk(CLK), .Q(x3q), .clr(R));
  Register #(.width(32)) x7 (.D(rd), .en(r7_we), .clk(CLK), .Q(x7q), .clr(R));
  Register #(.width(32)) x11 (.D(rd), .en(r11_we), .clk(CLK), .Q(x11q), .clr(R));
  Register #(.width(32)) x15 (.D(rd), .en(r15_we), .clk(CLK), .Q(x15q), .clr(R));
  Register #(.width(32)) x19 (.D(rd), .en(r19_we), .clk(CLK), .Q(x19q), .clr(R));
  Register #(.width(32)) x23 (.D(rd), .en(r23_we), .clk(CLK), .Q(x23q), .clr(R));
  Register #(.width(32)) x27 (.D(rd), .en(r27_we), .clk(CLK), .Q(x27q), .clr(R));
  Register #(.width(32)) x31 (.D(rd), .en(r31_we), .clk(CLK), .Q(x31q), .clr(R));
  Multiplexer #(.select(5), .width(32)) multiplexer_1 (
    .in0({32{1'b0}}), .in1(x1q), .in2(x2q), .in3(x3q), .in4(x4q), .in5(x5q), .in6(x6q), .in7(x7q), .in8(x8q),
    .in9(x9q), .in10(x10q), .in11(x11q), .in12(x12q), .in13(x13q), .in14(x14q), .in15(x15q), .in16(x16q),
    .in17(x17q), .in18(x18q), .in19(x19q), .in20(x20q), .in21(x21q), .in22(x22q), .in23(x23q), .in24(x24q),
    .in25(x25q), .in26(x26q), .in27(x27q), .in28(x28q), .in29(x29q), .in30(x30q), .in31(x31q), .out(rs1),
    .sel(rsi1));
  Multiplexer #(.select(5), .width(32)) multiplexer_2 (
    .in0({32{1'b0}}), .in1(x1q), .in2(x2q), .in3(x3q), .in4(x4q), .in5(x5q), .in6(x6q), .in7(x7q), .in8(x8q),
    .in9(x9q), .in10(x10q), .in11(x11q), .in12(x12q), .in13(x13q), .in14(x14q), .in15(x15q), .in16(x16q),
    .in17(x17q), .in18(x18q), .in19(x19q), .in20(x20q), .in21(x21q), .in22(x22q), .in23(x23q), .in24(x24q),
    .in25(x25q), .in26(x26q), .in27(x27q), .in28(x28q), .in29(x29q), .in30(x30q), .in31(x31q), .out(rs2),
    .sel(rsi2));

  // Notes on the sheet:
  //   x0
endmodule

module ALU (
  input  [31:0] dataA,
  input  [31:0] dataB,
  input  [3:0] sel,
  output [31:0] dataD
);

  wire comparator_1_lt, comparator_2_lt;
  wire [31:0] addOut, andOut, orOut, sllOut, sltOut, sltuOut, sraOut, srlOut, subOut, xorOut;

  Adder #(.width(32)) adder_1 (.a(dataA), .b(dataB), .out(addOut));  // open: cin, cout
  Subtractor #(.width(32)) subtractor_1 (.a(dataA), .b(dataB), .out(subOut));  // open: bin, bout
  Shifter #(.width(32)) shifter_1 (.in(dataA), .\dist (dataB[4:0]), .out(sllOut));
  Comparator #(.width(32)) comparator_1 (.a(dataA), .b(dataB), .lt(comparator_1_lt));  // open: gt, eq
  Comparator #(.mode("unsigned"), .width(32)) comparator_2 (
    .a(dataA), .b(dataB), .lt(comparator_2_lt));  // open: gt, eq
  assign xorOut = dataA ^ dataB;  // XOR_Gate xor_1, 32 bits wide
  Shifter #(.shift("lr"), .width(32)) shifter_2 (.in(dataA), .\dist (dataB[4:0]), .out(srlOut));
  Shifter #(.shift("ar"), .width(32)) shifter_3 (.in(dataA), .\dist (dataB[4:0]), .out(sraOut));
  assign orOut = dataA | dataB;  // OR_Gate or_1, 32 bits wide
  assign andOut = dataA & dataB;  // AND_Gate and_1, 32 bits wide
  assign sltOut = {{31{1'b0}}, comparator_1_lt};  // Bit_Extender bit_extender_1
  assign sltuOut = {{31{1'b0}}, comparator_2_lt};  // Bit_Extender bit_extender_2
  Multiplexer #(.select(4), .width(32)) multiplexer_1 (
    .in0(addOut), .in1(sllOut), .in2(sltOut), .in3(sltuOut), .in4(xorOut), .in5(srlOut), .in6(orOut),
    .in7(andOut), .in8(subOut), .in13(sraOut), .out(dataD), .sel(sel));  // open: in9, in10, in11, in12, in14, in15

  // Other names for the same wires on the sheet: dataBL5[4:0] = dataB[4:0]

  // Notes on the sheet:
  //   0000 add
  //   1000 sub
  //   0001 slt
  //   0010 slt
  //   0011 sltu
  //   0100 xor
  //   0101 srl
  //   1101 sra
  //   0110 or
  //   0111 and
endmodule

// ImmG
module ImmediateGenerator (
  input  [31:0] ins,
  input  [2:0] sel,
  output [31:0] imm31_0
);

  wire [3:0] bsplitter_1_imm4_1;
  wire [4:0] ssplitter_1_rdi;
  wire [5:0] bsplitter_1_imm10_5;
  wire [6:0] ssplitter_1_imm11_0;
  wire [7:0] jsplitter_1_imm19_12;
  wire [9:0] jsplitter_1_imm10_1;
  wire [11:0] isplitter_1_imm11_0;
  wire [12:11] bsplitter_1_imm11;
  wire [20:11] jsplitter_1_imm11;
  wire [31:0] BOut, IOut, JOut, SOut;
  wire [31:12] UOut;

  ISplitter isplitter_1 (.ins(ins), .imm11_0(isplitter_1_imm11_0));  // open: opcode, rdi, rsi1, funct3
  SSplitter ssplitter_1 (
    .ins(ins), .imm11_0(ssplitter_1_imm11_0), .rdi(ssplitter_1_rdi));  // open: opcode, rsi1, rsi2, funct3
  BSplitter bsplitter_1 (
    .ins(ins), .imm10_5(bsplitter_1_imm10_5), .imm4_1(bsplitter_1_imm4_1), .imm11(bsplitter_1_imm11[11]),
    .imm12(bsplitter_1_imm11[12]));  // open: opcode, rsi1, rsi2, funct3
  JSplitter jsplitter_1 (
    .ins(ins), .imm20(jsplitter_1_imm11[20]), .imm11(jsplitter_1_imm11[11]), .imm10_1(jsplitter_1_imm10_1),
    .imm19_12(jsplitter_1_imm19_12));  // open: opcode, rdi
  USplitter usplitter_1 (.ins(ins), .imm31_12(UOut));  // open: opcode, rdi
  assign IOut = {{20{isplitter_1_imm11_0[11]}}, isplitter_1_imm11_0};  // Bit_Extender bit_extender_1
  assign SOut = {{20{ssplitter_1_imm11_0[6]}}, {ssplitter_1_imm11_0, ssplitter_1_rdi}};  // Bit_Extender bit_extender_2
  assign BOut = {{19{bsplitter_1_imm11[12]}}, {bsplitter_1_imm11, bsplitter_1_imm10_5, bsplitter_1_imm4_1, 1'b0}};  // Bit_Extender bit_extender_3
  assign JOut = {{11{jsplitter_1_imm11[20]}}, {jsplitter_1_imm11[20], jsplitter_1_imm19_12, jsplitter_1_imm11[11], jsplitter_1_imm10_1, 1'b0}};  // Bit_Extender bit_extender_4
  Multiplexer #(.select(3), .width(32)) multiplexer_1 (
    .in0(IOut), .in1(SOut), .in2(BOut), .in3(JOut), .in4({UOut, {12{1'b0}}}), .out(imm31_0), .sel(sel));  // open: in5, in6, in7
endmodule

module RSplitter (
  input  [31:0] ins,
  output [6:0] opcode,
  output [4:0] rd,
  output [2:0] funct3,
  output [4:0] rs1,
  output [4:0] rs2,
  output [6:0] funct7
);


  assign funct3 = ins[14:12];
  assign funct7 = ins[31:25];
  assign opcode = ins[6:0];
  assign rd = ins[11:7];
  assign rs1 = ins[19:15];
  assign rs2 = ins[24:20];
endmodule

module ISplitter (
  input  [31:0] ins,
  output [6:0] opcode,
  output [4:0] rdi,
  output [2:0] funct3,
  output [4:0] rsi1,
  output [11:0] imm11_0
);


  assign funct3 = ins[14:12];
  assign imm11_0 = ins[31:20];
  assign opcode = ins[6:0];
  assign rdi = ins[11:7];
  assign rsi1 = ins[19:15];
endmodule

module SSplitter (
  input  [31:0] ins,
  output [6:0] opcode,
  output [4:0] rdi,
  output [2:0] funct3,
  output [4:0] rsi1,
  output [4:0] rsi2,
  output [6:0] imm11_0
);


  assign funct3 = ins[14:12];
  assign imm11_0 = ins[31:25];
  assign opcode = ins[6:0];
  assign rdi = ins[11:7];
  assign rsi1 = ins[19:15];
  assign rsi2 = ins[24:20];
endmodule

module BSplitter (
  input  [31:0] ins,
  output [6:0] opcode,
  output imm11,
  output [3:0] imm4_1,
  output [2:0] funct3,
  output [4:0] rsi1,
  output [4:0] rsi2,
  output [5:0] imm10_5,
  output imm12
);


  assign funct3 = ins[14:12];
  assign imm4_1 = ins[11:8];
  assign imm10_5 = ins[30:25];
  assign imm11 = ins[7];
  assign imm12 = ins[31];
  assign opcode = ins[6:0];
  assign rsi1 = ins[19:15];
  assign rsi2 = ins[24:20];
endmodule

module USplitter (
  input  [31:0] ins,
  output [6:0] opcode,
  output [4:0] rdi,
  output [19:0] imm31_12
);


  assign imm31_12 = ins[31:12];
  assign opcode = ins[6:0];
  assign rdi = ins[11:7];
endmodule

module JSplitter (
  input  [31:0] ins,
  output [6:0] opcode,
  output [4:0] rdi,
  output [7:0] imm19_12,
  output imm11,
  output [9:0] imm10_1,
  output imm20
);


  assign imm10_1 = ins[30:21];
  assign imm11 = ins[20];
  assign imm19_12 = ins[19:12];
  assign imm20 = ins[31];
  assign opcode = ins[6:0];
  assign rdi = ins[11:7];
endmodule

module Brancher (
  input  [31:0] dataA,
  input  [31:0] dataB,
  input  brUn,
  output brEq,
  output brLt
);

  wire comparator_1_lt, comparator_2_lt;

  Comparator #(.width(32)) comparator_1 (.a(dataA), .b(dataB), .eq(brEq), .lt(comparator_1_lt));  // open: gt
  Comparator #(.mode("unsigned"), .width(32)) comparator_2 (
    .a(dataA), .b(dataB), .lt(comparator_2_lt));  // open: gt, eq
  Multiplexer multiplexer_1 (.in0(comparator_1_lt), .in1(comparator_2_lt), .out(brLt), .sel(brUn));

  // Notes on the sheet:
  //   2's Complement
  //   Unsigned
endmodule

module datapath (
  input  in_1,
  output [31:0] out
);

  wire CLK, controllogic_1_bsel, regWe, wbSel;
  wire [2:0] immSel, lSel;
  wire [3:0] controllogic_1_alusel;
  wire [4:0] rdi, rsi1, rsi2;
  wire [7:0] bitselector_1_out, shifter_1_out;
  wire [23:0] pc_1_outpc, pc_1_outpcplus1;
  wire [31:0] aluctrl_1_datab, dataD, immediategenerator_1_imm31_0, ins, lw, registerfile_1_rs1,
       registerfile_1_rs2, rom_1_data;

  Clock clock_1 (.out(CLK));
  BitSelector #(.group(8), .width(32)) bitselector_1 (.in(out), .out(bitselector_1_out), .sel(2'b00));
  ROM #(.addrWidth(24), .dataWidth(32)) rom_1 (.addr(pc_1_outpc), .data(rom_1_data));
  PC pc_1 (.inPC(pc_1_outpcplus1), .CLK(CLK), .R(in_1), .outPCPlus1(pc_1_outpcplus1), .outPC(pc_1_outpc));
  RegisterFile registerfile_1 (
    .rsi2(rsi2), .rdi(rdi), .rd(dataD), .we(regWe), .CLK(CLK), .R(in_1), .rsi1(rsi1),
    .rs1(registerfile_1_rs1), .rs2(registerfile_1_rs2));
  ImmediateGenerator immediategenerator_1 (.sel(immSel), .ins(ins), .imm31_0(immediategenerator_1_imm31_0));
  ControlLogic controllogic_1 (
    .ins(ins), .aluSel(controllogic_1_alusel), .immSel(immSel), .bSel(controllogic_1_bsel), .wbSel(wbSel),
    .regWe(regWe), .lSel(lSel));
  Shifter #(.shift("lr")) shifter_1 (.in(bitselector_1_out), .\dist (3'b010), .out(shifter_1_out));
  ALUCtrl aluctrl_1 (
    .imm31_0(immediategenerator_1_imm31_0), .bSel(controllogic_1_bsel), .rs2(registerfile_1_rs2),
    .dataB(aluctrl_1_datab));
  RAM #(.dataWidth(32), .enables("line")) ram_1 (.addr(shifter_1_out), .clk(CLK), .dout(lw));  // open: we, din
  InstructionDecoder instructiondecoder_1 (.ins(rom_1_data), .rdi(rdi), .out_2(ins), .rs1(rsi1), .rs2(rsi2));
  ALU alu_1 (.sel(controllogic_1_alusel), .dataB(aluctrl_1_datab), .dataA(registerfile_1_rs1), .dataD(out));
  LoadCtrl loadctrl_1 (.lw(lw), .lSel(lSel), .rbSel(wbSel), .A(out), .D(dataD));

  // Other names for the same wires on the sheet: aluOut[31:0] = out; R = in_1

  // Notes on the sheet:
  //   contents of rom_1 (hex, n*v repeats v):
  //   a00293 1400313 6283b3 400193 218103
endmodule

module ControlLogic (
  input  [31:0] ins,
  output [3:0] aluSel,
  output regWe,
  output [2:0] immSel,
  output bSel,
  output wbSel,
  output [2:0] lSel
);

  ROM #(.addrWidth(9), .dataWidth(13)) rom_1 (
    .addr({ins[30], ins[14:12], ins[6:2]}), .data({lSel, wbSel, aluSel, regWe, immSel, bSel}));

  // Other names for the same wires on the sheet: i2 = ins[2]; i3 = ins[3]; i4 = ins[4]; i5 = ins[5]; i6 = ins[6];
  //   i12 = ins[12]; i13 = ins[13]; i14 = ins[14]; i30 = ins[30]; as0 = aluSel[0]; as1 = aluSel[1]; as2 = aluSel[2];
  //   as3 = aluSel[3]; is0 = immSel[0]; is1 = immSel[1]; is2 = immSel[2]

  // Notes on the sheet:
  //   contents of rom_1 (hex, n*v repeats v):
  //   11 0 0 0 211 7*0 210 19*0 411 0 0 0 231 7*0 230 19*0 811 0 0 0 251 7*0 250 23*0 271 7*0 270 19*0
  //   1011 0 0 0 291 7*0 290 19*0 1411 0 0 0 2b1 7*0 2b0 23*0 2d1 7*0 2d0 23*0 2f1 7*0 2f0 31*0 310 151*0
  //   3b1 7*0 3b0
endmodule

module ALUCtrl (
  input  [31:0] rs2,
  input  [31:0] imm31_0,
  input  bSel,
  output [31:0] dataB
);

  Multiplexer #(.width(32)) multiplexer_1 (.in0(rs2), .in1(imm31_0), .out(dataB), .sel(bSel));
endmodule

// InsDecoder
module InstructionDecoder (
  input  [31:0] ins,
  output [31:0] out_2,
  output [4:0] rs1,
  output [4:0] rs2,
  output [4:0] rdi
);


  assign out_2 = ins;
  assign rdi = ins[11:7];
  assign rs1 = ins[19:15];
  assign rs2 = ins[24:20];
endmodule

// LB
module LoadByte (
  input  [31:0] A,
  input  [31:0] lw,
  output [31:0] lb,
  output [31:0] lbu
);

  wire [4:0] bitselector_1_out;
  wire [7:0] bitselector_2_out;
  wire [31:0] and_1_out, shifter_1_out, shifter_2_out, subtractor_1_out;

  assign and_1_out = A & 32'h3;  // AND_Gate and_1, 32 bits wide
  Subtractor #(.width(32)) subtractor_1 (.a(32'h3), .b(and_1_out), .out(subtractor_1_out));  // open: bin, bout
  BitSelector #(.group(5), .width(32)) bitselector_1 (.in(shifter_1_out), .out(bitselector_1_out), .sel(3'b000));
  Shifter #(.width(32)) shifter_1 (.in(subtractor_1_out), .\dist (5'b00011), .out(shifter_1_out));
  Shifter #(.shift("lr"), .width(32)) shifter_2 (.in(lw), .\dist (bitselector_1_out), .out(shifter_2_out));
  BitSelector #(.group(8), .width(32)) bitselector_2 (.in(shifter_2_out), .out(bitselector_2_out), .sel(2'b00));
  assign lbu = shifter_2_out & 32'hff;  // AND_Gate and_2, 32 bits wide
  assign lb = {{24{bitselector_2_out[7]}}, bitselector_2_out};  // Bit_Extender bit_extender_1
endmodule

// LHW
module LoadHalfWord (
  input  [31:0] A,
  input  [31:0] lw,
  output [31:0] lh,
  output [31:0] lhu
);

  wire bitselector_1_out, not_1_out;
  wire [15:0] bitselector_2_out;

  BitSelector #(.width(32)) bitselector_1 (.in(A), .out(bitselector_1_out), .sel(5'b00001));
  BitSelector #(.group(16), .width(32)) bitselector_2 (.in(lw), .out(bitselector_2_out), .sel(not_1_out));
  not not_1 (not_1_out, bitselector_1_out);
  assign lh = {{16{bitselector_2_out[15]}}, bitselector_2_out};  // Bit_Extender bit_extender_1
  assign lhu = {{16{1'b0}}, bitselector_2_out};  // Bit_Extender bit_extender_2
endmodule

module LoadCtrl (
  input  [31:0] A,
  input  [31:0] lw,
  input  [2:0] lSel,
  input  rbSel,
  output [31:0] D
);

  wire [31:0] lb, lbu, lh, lhu, multiplexer_1_out;

  LoadByte loadbyte_1 (.lw(lw), .A(A), .lb(lb), .lbu(lbu));
  LoadHalfWord loadhalfword_1 (.lw(lw), .A(A), .lh(lh), .lhu(lhu));
  Multiplexer #(.select(3), .width(32)) multiplexer_1 (
    .in0(lb), .in1(lh), .in2(lw), .in4(lbu), .in5(lhu), .out(multiplexer_1_out), .sel(lSel));  // open: in3, in6, in7
  Multiplexer #(.width(32)) multiplexer_2 (.in0(multiplexer_1_out), .in1(A), .out(D), .sel(rbSel));
endmodule
